# Fritzing sketch usb-keyboard (saved by Fritzing 0.9.3b)

parts:
  Mod1 = Raspberry Pi Pico
  A1 = Waveshare rp2040-zero tht [package=THT]
  Mod2 = Raspberry Pi Pico
  Mod3 = Raspberry Pi Pico

nets:
  N1: Mod1.pin_1, A1.Pin_22
  N2: Mod1.pin_2, A1.Pin_23
  N3: Mod1.pin_33, Mod1.pin_38, A1.Pin_2
  N4: Mod1.pin_40, A1.Pin_1
  N5: Mod2.pin_1, Mod3.pin_2
  N6: Mod2.pin_2, Mod3.pin_1
  N7: Mod2.pin_39, Mod3.pin_3, Mod3.pin_42
  N8: Mod2.pin_40, Mod3.pin_40

notes:
  CPU
  KBD
  USB C Variant does not require adapter
  Requires USB A - Micro Adapter

custom parts:
  Raspberry Pi Pico: Raspberry Pi Pico. Based around the RP2040 microcontroller the Pico is a low cost microcontroller device bringing Raspberry Pi quality, cost, and easy of use to the microcontroller space. Jan 2021, Split part in to two versions: tht (this one) and SMD. This one will drill holes for a .1 in header in pcb to allow plugging in the module as well as providing pads to solder the module to the top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
  Waveshare rp2040-zero tht: .RP2040-Zero, A Low-Cost, High-Performance Pico-Like MCU Board Based On Raspberry Pi Microcontroller RP2040. This varant is THT without the extra connections.
